# Fritzing sketch solar_tracker_fritzing (saved by Fritzing 0.9.2b)
circuit board: 8.46667cm x 5.64444cm
breadboards: 1

parts:
  IC3 = IC, DIP package, 14 pins [chip_label=ATTiny24/44/84]
  IC4 = L293D [package=THT]
  Left_LDR = Photocell (LDR) [package=THT]
  RIGHT_LDR = Photocell (LDR) [package=THT]
  R3 = Resistor [tolerance=±5% resistance=10k package=THT]
  R4 = Resistor [tolerance=±5% resistance=10k package=THT]
  R5 = Resistor [tolerance=±5% resistance=10k package=THT]
  R6 = Resistor [tolerance=±5% resistance=10k package=THT]
  M1 = DC Motor
  D1 = Diode [package=diode-1n4148]
  D2 = Diode [package=diode-1n4148]
  D3 = Diode [package=diode-1n4148]
  D4 = Diode [package=diode-1n4148]
  Open_End_Stop = D2F-FL Omron Snap Action Limit Switch with Level
  Close_End_Stop = D2F-FL Omron Snap Action Limit Switch with Level
  POWER_IN = Screw terminal - 2 pins [package=THT]
  GROUND_IN = Screw terminal - 2 pins [package=THT]
  220uF = Capacitor Polarized [package=cpol-radial-1000uf-25v]

nets:
  5V: IC3.pin1, IC4.Enable_1, Left_LDR.pin_0, RIGHT_LDR.pin_0, R5.Pin_1, R6.Pin_1, POWER_IN.pin1, 220uF.+
  N1: IC3.pin2, IC4.In_2
  N2: IC3.pin3, IC4.In_1
  N3: IC3.pin5, R5.Pin_0, Open_End_Stop.NO
  N4: IC3.pin6, R6.Pin_0, Close_End_Stop.NO
  N5: IC3.pin11, Left_LDR.pin_1, R4.Pin_0
  N6: IC3.pin12, RIGHT_LDR.pin_1, R3.Pin_0
  GND: IC3.pin14, IC4.0V, R3.Pin_1, R4.Pin_1, D2.A, D4.A, Open_End_Stop.COM, Close_End_Stop.COM, GROUND_IN.pin1, 220uF.-
  N7: IC4.Out_1_(_Controlled_by_Enable_1_), M1.pin_1, D1.A, D2.C
  N8: IC4.Out_2_(_Controlled_by_Enable_1_), M1.pin_2, D3.A, D4.C
  12V: IC4.+Vmotor, D1.C, D3.C, POWER_IN.pin2

custom parts:
  D2F-FL Omron Snap Action Limit Switch with Level: sealed stainless steel lever SPDT Microswitch.
